# Fritzing sketch IR LED Sequencer (saved by Fritzing 0.9.3b)
breadboards: 1

parts:
  Part1 = Arduino Uno (Rev3)
  LED1 = LED - 5mm [color="Green (565nm)" package="5 mm [THT]"]
  LED2 = LED - 5mm [color="Green (565nm)" package="5 mm [THT]"]
  LED3 = LED - 5mm [color="Green (565nm)" package="5 mm [THT]"]
  LED4 = LED - 5mm [color="Green (565nm)" package="5 mm [THT]"]
  U1 = mystery part, 3 pins [chip_label=TSOP]
  R1 = Resistor [tolerance=±5% resistance=100 package=THT]
  C1 = Tantalum Capacitor [capacitance=0.1µF package="100 mil [THT, tantalum]"]
  R4 = Resistor [tolerance=±5% resistance=82 package=THT]

nets:
  N1: Part1.D8, LED4.anode
  N2: Part1.D9_PWM, LED3.anode
  N3: Part1.D10_PWM/SS, LED2.anode
  N4: Part1.D11_PWM/MOSI, LED1.anode
  N5: Part1.D2, U1.pin3
  N6: Part1.5V, R1.Pin_0
  N7: Part1.GND, U1.pin2, C1.-, R4.Pin_0
  N8: LED1.cathode, R4.Pin_1
  N9: U1.pin1, R1.Pin_1, C1.+

notes:
  0.1µF
