# Fritzing sketch AccelerometerTest (saved by Fritzing 0.9.3b)
breadboards: 1

parts:
  Part1 = Arduino Uno (Rev3)
  Part2 = LCD Keypad Shield  # not connected
  GY1 = MPU-6050 Board GY-521 [form="♀ (female)" package=THT]

nets:
  N1: Part1.A4/SDA, GY1.pin4, GY1.pin5
  N2: Part1.A5/SCL, GY1.pin3
  N3: Part1.5V, GY1.pin1
  N4: Part1.GND, GY1.pin2

custom parts:
  LCD Keypad Shield: It consists of a 1602 white character blue backlight LCD. The keypad consists of 5 keys — select, up, right, down and left. To save the digital IO pins, the keypad interface uses only one ADC channel. The key value is read through a 5 stage voltage divider.
  MPU-6050 Board GY-521: Acelerometro y Giroscopio MPU-6050 Board GY-521
