# Fritzing sketch StepperSerial (saved by Fritzing 0.9.3b)
breadboards: 1

parts:
  Part1 = Arduino Uno (Rev3)
  Power_plug1 = Power plug
  ULN2003A_-_Stepper_Driver_Board1 = ULN2003A - Stepper Driver Board [package=board]
  MOTOR1 = 28BYJ-48 Stepper Motor

nets:
  N1: Part1.D2, ULN2003A_-_Stepper_Driver_Board1.IN1
  N2: Part1.D3_PWM, ULN2003A_-_Stepper_Driver_Board1.IN2
  N3: Part1.D4, ULN2003A_-_Stepper_Driver_Board1.IN3
  N4: Part1.D5_PWM, ULN2003A_-_Stepper_Driver_Board1.IN4
  GND: Power_plug1.GND, ULN2003A_-_Stepper_Driver_Board1.GND
  VCC: Power_plug1.VCC, ULN2003A_-_Stepper_Driver_Board1.VCC
  N5: ULN2003A_-_Stepper_Driver_Board1.BLUE, MOTOR1.RED
  N6: ULN2003A_-_Stepper_Driver_Board1.PINK, MOTOR1.ORANGE
  N7: ULN2003A_-_Stepper_Driver_Board1.YELLOW, MOTOR1.YELLOW
  N8: ULN2003A_-_Stepper_Driver_Board1.ORANGE, MOTOR1.PINK
  N9: ULN2003A_-_Stepper_Driver_Board1.RED, MOTOR1.BLUE

custom parts:
  ULN2003A - Stepper Driver Board: A common stepper motor driver board based on ULN2003APG darlington array
