# Fritzing sketch UltrasonicTestImproved (saved by Fritzing 0.9.3b)
breadboards: 1

parts:
  Part1 = Arduino Uno (Rev3)
  Part2 = LCD Keypad Shield  # not connected
  Part3 = HC-SR04

nets:
  N1: Part1.D10_PWM/SS, Part3.Echo
  N2: Part1.D11_PWM/MOSI, Part3.Trig
  5V: Part1.5V, Part3.Vcc
  GND: Part1.GND, Part3.Gnd

custom parts:
  LCD Keypad Shield: It consists of a 1602 white character blue backlight LCD. The keypad consists of 5 keys — select, up, right, down and left. To save the digital IO pins, the keypad interface uses only one ADC channel. The key value is read through a 5 stage voltage divider.
  HC-SR04: HC-SR04 ultrasonic distance sensor
