# Fritzing sketch UNORobotHypothetical (saved by Fritzing 0.9.3b)
breadboards: 1

parts:
  Power_plug1 = Power plug
  U2 = ESP8266 ESP-01 Upgraded WiFi Module [part_number=ESP8266]
  R1 = Resistor [tolerance=±5% resistance=10k package=THT]
  S2 = Pushbutton [package="[THT]"]
  R2 = Resistor [tolerance=±5% resistance=2.2k package=THT]
  R3 = Resistor [tolerance=±5% resistance=2.2k package=THT]
  R4 = Resistor [tolerance=±5% resistance=2.2k package=THT]
  R5 = Resistor [tolerance=±5% resistance=2.2k package=THT]
  R6 = Resistor [tolerance=±5% resistance=2.2k package=THT]
  R7 = Resistor [tolerance=±5% resistance=2.2k package=THT]
  S3 = Pushbutton [package="[THT]"]
  R8 = Resistor [tolerance=±5% resistance=10k package=THT]
  R9 = Resistor [tolerance=±5% resistance=2.2k package=THT]
  R10 = Resistor [tolerance=±5% resistance=2.2k package=THT]
  R11 = Resistor [tolerance=±5% resistance=2.2k package=THT]
  D1 = Rectifier Diode [part_number=1N4001 package="300 mil [THT]"]
  C1 = Electrolytic Capacitor [capacitance=1µF package="100 mil [THT, electrolytic]"]
  U3 = Voltage Regulator - 5V [package="TO220 [THT]"]
  C2 = Electrolytic Capacitor [capacitance=4.7µF package="100 mil [THT, electrolytic]"]
  J1 = Basic Servo
  M1 = DC Motor
  M2 = DC Motor
  S4 = H-Bridge with L298N
  LCD1 = LCD screen
  Part2 = HC-SR04
  TCRT11 = TCRT5000 digital module [part_number=151608]
  TCRT12 = TCRT5000 digital module [part_number=151608]
  TCRT13 = TCRT5000 digital module [part_number=151608]
  TCRT14 = TCRT5000 digital module [part_number=151608]
  TCRT15 = TCRT5000 digital module [part_number=151608]
  LCM1602_IIC1 = LCM1602 IIC [part_number="LCM1602 IIC" chip_label="LCM1602 IIC" package="DIP (Dual Inline) [THT]"]
  Part3 = Arduino Uno (Rev3)

nets:
  GND: Power_plug1.GND, U2.GPIO_0, U2.GND, S2.Pin_1, S2.Pin_2, R2.Pin_0, R5.Pin_0, S3.Pin_3, S3.Pin_4, R8.Pin_1, R9.Pin_0, C1.+, U3.GND, J1.gnd, S4.GND, Part2.Gnd, TCRT11.GND, TCRT12.GND, TCRT13.GND, TCRT14.GND, TCRT15.GND, LCM1602_IIC1.GND
  VCC: Power_plug1.VCC, D1.anode, J1.vcc, S4.5V, Part2.Vcc, TCRT11.VCC, TCRT12.VCC, TCRT13.VCC, TCRT14.VCC, TCRT15.VCC, LCM1602_IIC1.VCC
  N1: U2.RXD, R10.Pin_1, R11.Pin_1
  N2: U2.VCC, R1.Pin_0, R8.Pin_0, C2.+
  N3: U2.RST/GPIO_16, R6.Pin_1, R7.Pin_0
  N4: U2.CH_PD, R3.Pin_1, R4.Pin_1
  N5: U2.TXD, Part3.D13/SCK
  N6: R1.Pin_1, S2.Pin_3, S2.Pin_4
  N7: R2.Pin_1, R3.Pin_0
  N8: R5.Pin_1, R6.Pin_0
  N9: R9.Pin_1, R10.Pin_0
  N10: R11.Pin_0, Part3.D12/MISO
  N11: D1.cathode, C1.-, U3.input_voltage
  N12: U3.output_voltage, C2.-
  N13: J1.pulse, Part3.D5_PWM
  N14: M1.pin_1, S4.M1-02
  N15: M1.pin_2, S4.M1-01
  N16: M2.pin_1, S4.M2-02
  N17: M2.pin_2, S4.M2-01
  N18: S4.ENA, Part3.D11_PWM/MOSI
  N19: S4.IN1, Part3.D10_PWM/SS
  N20: S4.IN2, Part3.D9_PWM
  N21: S4.IN3, Part3.D8
  N22: S4.IN4, Part3.D7
  N23: S4.ENB, Part3.D6_PWM
  VSS: LCD1.VSS, LCM1602_IIC1.VSS
  VDD: LCD1.VDD, LCM1602_IIC1.VDD
  N24: LCD1.V0, LCM1602_IIC1.V0
  N25: LCD1.RS, LCM1602_IIC1.RS
  N26: LCD1.R/W, LCM1602_IIC1.RW
  N27: LCD1.E, LCM1602_IIC1.E
  N28: LCD1.DB0, LCM1602_IIC1.D0
  N29: LCD1.DB1, LCM1602_IIC1.D1
  N30: LCD1.DB2, LCM1602_IIC1.D2
  N31: LCD1.DB3, LCM1602_IIC1.D3
  N32: LCD1.DB4, LCM1602_IIC1.D4
  N33: LCD1.DB5, LCM1602_IIC1.D5
  N34: LCD1.DB6, LCM1602_IIC1.D6
  N35: LCD1.DB7, LCM1602_IIC1.D7
  N36: LCD1.LED+, LCM1602_IIC1.A
  N37: LCD1.LED-, LCM1602_IIC1.K
  N38: Part2.Trig, Part3.D4
  N39: Part2.Echo, Part3.D3_PWM
  N40: TCRT11.DO2, Part3.A0
  N41: TCRT12.DO2, Part3.A2
  N42: TCRT13.DO2, LCM1602_IIC1.SDA, Part3.A4/SDA
  N43: TCRT14.DO2, Part3.A1
  N44: TCRT15.DO2, Part3.A3
  N45: LCM1602_IIC1.SCL, Part3.A5/SCL

notes:
  3.3V
  4.7µF
  1µF
  5V
  Good luck

custom parts:
  ESP8266 ESP-01 Upgraded WiFi Module: Upgraded Version ESP-01,all Flash are upgraded to 1M byte.Also support Cloud service remote transmission.
  H-Bridge with L298N: h-bridge
  HC-SR04: HC-SR04 ultrasonic distance sensor
  TCRT5000 digital module: breakout board for TCRT5000 module, convert analog to digital - Uses TCRT5000 infrared reflectance sensor - Detection distance: 1mm~8mm - Focus distance: 2.5mm - Working voltage: 3.3V~12V - Uses wide voltage LM393 comparator - With multi-turn precision potentiometer to adjust the sensitivity - Current: > 15mA - Output type: Digital switch output (0, 1) - Suitable for watt-hour meter pulse data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
  LCM1602 IIC: I2C-Module to use a 1602 or 2004 LCD on with the wire.h libory Serial LCD Modul
