# Fritzing sketch Wifi (saved by Fritzing 0.9.3b)
breadboards: 1

parts:
  VCC1 = Battery
  Part3 = Arduino Uno (Rev3)
  U1 = ESP8266 ESP-01 Upgraded WiFi Module [part_number=ESP8266]
  R1 = Resistor [tolerance=±5% resistance=10k package=THT]
  R2 = Resistor [tolerance=±5% resistance=10k package=THT]
  R3 = Resistor [tolerance=±5% resistance=10k package=THT]
  U2 = Voltage Regulator - 3.3V [package="TO220 [THT]"]

nets:
  GND: VCC1.-, Part3.GND, U1.GPIO_0, U1.GND, R2.Pin_0, U2.GND
  N1: VCC1.+, U2.input_voltage
  N2: Part3.D0/RX, U1.RXD
  N3: Part3.D1/TX, R3.Pin_1
  N4: U1.CH_PD, U2.output_voltage
  N5: U1.TXD, R1.Pin_1, R3.Pin_0
  N6: R1.Pin_0, R2.Pin_1

custom parts:
  ESP8266 ESP-01 Upgraded WiFi Module: Upgraded Version ESP-01,all Flash are upgraded to 1M byte.Also support Cloud service remote transmission.
