# Fritzing sketch WeatherStation (saved by Fritzing 0.9.3b)
breadboards: 1

parts:
  Nokia_5110_LCD_Module1 = Nokia 5110 LCD basado en PCD8544
  Part1 = Arduino Uno (Rev3) - ICSP
  DHT1 = DHT22 Humidity and Temperature Sensor
  Part2 = Adafruit DS3231 [part_number="Adafruit #3013"]

nets:
  VCC: Nokia_5110_LCD_Module1.VCC, Nokia_5110_LCD_Module1.LIGHT, Part1.3V3
  GND: Nokia_5110_LCD_Module1.GND, Part1.GND, DHT1.GND, Part2.GND
  N1: Nokia_5110_LCD_Module1.CE, Part1.ICSP_MISO, Part1.D12/MISO
  N2: Nokia_5110_LCD_Module1.RST, Part1.D11_PWM/MOSI
  N3: Nokia_5110_LCD_Module1.DC, Part1.D10_PWM/SS
  N4: Nokia_5110_LCD_Module1.DIN, Part1.D9_PWM
  N5: Nokia_5110_LCD_Module1.CLK, Part1.D8
  N6: Part1.A4/SDA, Part2.SDA
  N7: Part1.A5/SCL, Part2.SCL
  N8: Part1.D2, DHT1.DATA
  5V: Part1.5V, DHT1.VDD, Part2.Vin

notes:
  I used a generic clone DS3231, but the pin out labled on the Adafruit board are the same.

custom parts:
  Nokia 5110 LCD basado en PCD8544: Módulo Nokia 5110 LCD basado en el controlador PCD8544. Versión de 8 pines (sólo entrada).
  Adafruit DS3231: The datasheet for the DS3231 explains that this part is an "Extremely Accurate I²C-Integrated RTC/TCXO/Crystal". And, hey, it does exactly what it says on the tin! This Real Time Clock (RTC) is the most precise you can get in a small, low power package. Most RTCs use an external 32kHz timing crystal that is used to keep time with low current draw. And that's all well and good, but those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
