# Fritzing sketch LCD_I2C_Ultrasonic_Test (saved by Fritzing 0.9.3b)

parts:
  Part1 = HC-SR04
  LCM1602_IIC1 = LCM1602 IIC [part_number="LCM1602 IIC" chip_label="LCM1602 IIC" package="DIP (Dual Inline) [THT]"]
  Part2 = Arduino Uno (Rev3) - ICSP

nets:
  VCC: Part1.Vcc, LCM1602_IIC1.VCC, Part2.5V
  N1: Part1.Trig, Part2.ICSP_MISO, Part2.D12/MISO
  N2: Part1.Echo, Part2.D11_PWM/MOSI
  GND: Part1.Gnd, LCM1602_IIC1.GND, Part2.GND
  N3: LCM1602_IIC1.SDA, Part2.A4/SDA
  N4: LCM1602_IIC1.SCL, Part2.A5/SCL

custom parts:
  HC-SR04: HC-SR04 ultrasonic distance sensor
  LCM1602 IIC: I2C-Module to use a 1602 or 2004 LCD on with the wire.h libory Serial LCD Modul
