# Fritzing sketch esp8266 (saved by Fritzing 0.9.3b)
breadboards: 1

parts:
  Part1 = Arduino Mega 2560 (Rev3)
  Power_plug1 = Power plug
  U2 = ESP8266 ESP-01 Upgraded WiFi Module [part_number=ESP8266]
  R1 = Resistor [tolerance=±5% resistance=10k package=THT]
  S2 = Pushbutton [package="[THT]"]
  R2 = Resistor [tolerance=±5% resistance=2.2k package=THT]
  R3 = Resistor [tolerance=±5% resistance=2.2k package=THT]
  R4 = Resistor [tolerance=±5% resistance=2.2k package=THT]
  R5 = Resistor [tolerance=±5% resistance=2.2k package=THT]
  R6 = Resistor [tolerance=±5% resistance=2.2k package=THT]
  R7 = Resistor [tolerance=±5% resistance=2.2k package=THT]
  S3 = Pushbutton [package="[THT]"]
  R8 = Resistor [tolerance=±5% resistance=10k package=THT]
  R9 = Resistor [tolerance=±5% resistance=2.2k package=THT]
  R10 = Resistor [tolerance=±5% resistance=2.2k package=THT]
  R11 = Resistor [tolerance=±5% resistance=2.2k package=THT]
  LED1 = LED - 5mm [color="Red (633nm)" package="5 mm [THT]"]
  LED2 = LED - 5mm [color="Green (565nm)" package="5 mm [THT]"]
  R12 = Resistor [tolerance=±5% resistance=1k package=THT]
  R13 = Resistor [tolerance=±5% resistance=1k package=THT]
  D1 = Rectifier Diode [part_number=1N4001 package="300 mil [THT]"]
  C1 = Electrolytic Capacitor [capacitance=1µF package="100 mil [THT, electrolytic]"]
  U3 = Voltage Regulator - 5V [package="TO220 [THT]"]
  C2 = Electrolytic Capacitor [capacitance=4.7µF package="100 mil [THT, electrolytic]"]

nets:
  N1: Part1.D19/RX1, R11.Pin_0
  N2: Part1.D18/TX1, U2.TXD
  N3: Part1.D8_PWM, LED2.anode
  N4: Part1.D2_PWM, R4.Pin_0
  N5: Part1.D3_PWM, R7.Pin_1
  N6: Part1.D7_PWM, LED1.anode
  GND: Power_plug1.GND, U2.GPIO_0, U2.GND, S2.Pin_1, S2.Pin_2, R2.Pin_0, R5.Pin_0, S3.Pin_3, S3.Pin_4, R8.Pin_1, R9.Pin_0, C1.+, U3.GND
  N7: Power_plug1.VCC, D1.anode
  N8: U2.RXD, R10.Pin_1, R11.Pin_1
  N9: U2.VCC, R1.Pin_0, R8.Pin_0, C2.+
  N10: U2.RST/GPIO_16, R6.Pin_1, R7.Pin_0
  N11: U2.CH_PD, R3.Pin_1, R4.Pin_1
  N12: R1.Pin_1, S2.Pin_3, S2.Pin_4
  N13: R2.Pin_1, R3.Pin_0
  N14: R5.Pin_1, R6.Pin_0
  N15: R9.Pin_1, R10.Pin_0
  N16: LED1.cathode, R12.Pin_0
  N17: LED2.cathode, R13.Pin_0
  N18: R12.Pin_1, R13.Pin_1
  N19: D1.cathode, C1.-, U3.input_voltage
  N20: U3.output_voltage, C2.-

notes:
  3.3V
  4.7µF
  1µF

custom parts:
  ESP8266 ESP-01 Upgraded WiFi Module: Upgraded Version ESP-01,all Flash are upgraded to 1M byte.Also support Cloud service remote transmission.
